// Logisim project Stop-countera.circ as structural Verilog: 1 circuit, main circuit main
module main (
);

  wire button_1_out, clock_1_out, counter_1_carry, d_ff_1_q, d_ff_2_q, or_1_out;

  Clock clock_1 (.out(clock_1_out));
  or or_1 (or_1_out, d_ff_2_q, clock_1_out);
  Button button_1 (.out(button_1_out));
  Counter #(.width(3), .max('h7)) counter_1 (.carry(counter_1_carry), .clk(or_1_out));  // open: load, D, count, Q, clr
  D_Flip_Flop d_ff_1 (.clk(or_1_out), .D(counter_1_carry), .Q(d_ff_1_q), .reset(button_1_out));  // open: Qn, preset, en
  D_Flip_Flop d_ff_2 (.Q(d_ff_2_q), .preset(d_ff_1_q), .reset(button_1_out));  // open: clk, D, Qn, en
endmodule
