// Logisim project Key_recognition.circ as structural Verilog: 1 circuit, main circuit main
module main (
  input  [6:0] Keyboard_input,
  input  Clk,
  output A,
  output [1:0] Out,
  output D
);

  wire and_1_out, comparator_1_eq, comparator_2_eq, comparator_3_eq, comparator_4_eq, or_3_out;

  Comparator #(.width(7)) comparator_1 (.a(Keyboard_input), .b(7'b1100001), .eq(comparator_1_eq));  // open: gt, lt
  Comparator #(.width(7)) comparator_2 (.a(Keyboard_input), .b(7'b1000001), .eq(comparator_2_eq));  // open: gt, lt
  Comparator #(.width(7)) comparator_3 (.a(Keyboard_input), .b(7'b1100100), .eq(comparator_3_eq));  // open: gt, lt
  Comparator #(.width(7)) comparator_4 (.a(Keyboard_input), .b(7'b1000100), .eq(comparator_4_eq));  // open: gt, lt
  or or_1 (A, comparator_1_eq, comparator_2_eq);
  or or_2 (D, comparator_3_eq, comparator_4_eq);
  or or_3 (or_3_out, D, A);
  and and_1 (and_1_out, or_3_out, Clk);
  Register #(.width(2)) register_1 (.D({A, D}), .Q(Out), .clk(and_1_out));  // open: en, clr

  // Notes on the sheet:
  //   A key
  //   D key
  //   Space
endmodule
