// Logisim project ROM_Tree.circ as structural Verilog: 1 circuit, main circuit main
module main (
  input  [2:0] Counter,
  output [23:0] ROM_0,
  output [23:0] ROM_1,
  output [23:0] ROM_2
);

  ROM #(.addrWidth(3), .dataWidth(24)) u_rom_1 (.addr(Counter), .data(ROM_0));  // open: sel
  ROM #(.addrWidth(3), .dataWidth(24)) u_rom_2 (.addr(Counter), .data(ROM_1));  // open: sel
  ROM #(.addrWidth(3), .dataWidth(24)) rom_3 (.addr(Counter), .data(ROM_2));  // open: sel

  // Notes on the sheet:
  //   contents of rom_1 (hex, n*v repeats v):
  //   8*7e00
  //   contents of rom_2 (hex, n*v repeats v):
  //   7e00 7e08 7f1c 7ffe 7f9c 7e08 7e00 7e00
  //   contents of rom_3 (hex, n*v repeats v):
  //   7e00 10fe00 38fe00 7ffe00 39fe00 107e00 7e00 7e00
endmodule
