// Logisim project main_pomysly.circ as structural Verilog: 1 circuit, main circuit main
module main (
  input  [2:0] in_1
);

  wire A, Alien, and_2_out, button_4_out, CLK_ANIM, CLK_IN, clock_1_out, comparator_2_eq, D, d_ff_1_q,
       d_ff_1_qn, d_ff_2_q, d_ff_3_q, d_ff_3_qn, Display_ready, Key_impulse, keyboard_1_avail, linia1,
       main_2_clk_out, main_3_clk_out, main_4_clk_out, main_5_clk_out, main_13_clk_timebar, Main_clk_out,
       Napoleon, not_1_out, not_2_out, or_1_out, or_3_out, or_4_out, pull_resistor_1_node, RESET, RstRgr,
       Scored, Timber, TIMEOUT;
  wire [1:0] key, main_1_out;
  wire [2:0] bit_extender_1_out, Counter, divider_1_rem, Kolizja_tree, random_1_out, shift_register_1_out,
       SR1, SR2, SR3, SR4, SR5;
  wire [3:0] H1, H2, H3, H4, HS1, HS2, HS3, HS4;
  wire [6:0] keyboard_1_data;
  wire [13:0] Points_value;
  wire [23:0] main_2_o0, main_2_o1, main_2_o2, main_2_o3, main_2_o4, main_2_o5, main_2_o6, main_2_o7,
       main_2_register_out, main_3_out_0, main_3_out_1, main_3_out_2, main_3_out_3, main_3_out_4,
       main_3_out_5, main_3_out_6, main_3_out_7, main_3_reg_out, main_4_o0, main_4_o1, main_4_o2, main_4_o3,
       main_4_o4, main_4_o5, main_4_o6, main_4_o7, main_4_register_out, main_5_out_0, main_5_out_1,
       main_5_out_2, main_5_out_3, main_5_out_4, main_5_out_5, main_5_out_6, main_5_out_7, main_5_reg_out,
       main_6_out_0, main_6_out_1, main_6_out_2, main_6_out_3, main_6_out_4, main_6_out_5, main_6_out_6,
       main_6_out_7, RegOut, ROM0, ROM1, ROM2, ROM_3, ROM_4;
  wire [31:0] Timer;

  or or_1 (or_1_out, Key_impulse, RstRgr);
  Skin_selectAND_main main_1 (._0(Timber), ._1(Napoleon), ._2(Alien), .out(main_1_out));
  Screen_animation_segment_main main_2 (
    .Input_line(RegOut), .Impulse(Key_impulse), .Reset(RstRgr), .O0(main_2_o0), .O1(main_2_o1),
    .O2(main_2_o2), .Register_out(main_2_register_out), .O3(main_2_o3), .O4(main_2_o4), .O5(main_2_o5),
    .O6(main_2_o6), .O7(main_2_o7), .Clk_out(main_2_clk_out), .Clk(CLK_ANIM));
  Over_screen_main main_3 (
    .Animation_Clock(main_2_clk_out), .Key_impulse(Key_impulse), .Reset__tree(RstRgr), .Out_0(main_3_out_0),
    .Out_1(main_3_out_1), .Out_2(main_3_out_2), .Out_3(main_3_out_3), .Out_4(main_3_out_4),
    .Out_5(main_3_out_5), .Out_6(main_3_out_6), .Out_7(main_3_out_7), .Input(main_2_register_out),
    .in_5(RstRgr), .Clk_out(main_3_clk_out), .Reg_out(main_3_reg_out));
  Screen_animation_segment_main main_4 (
    .Input_line(main_3_reg_out), .Impulse(Key_impulse), .Reset(RstRgr), .O0(main_4_o0), .O1(main_4_o1),
    .O2(main_4_o2), .Register_out(main_4_register_out), .O3(main_4_o3), .O4(main_4_o4), .O5(main_4_o5),
    .O6(main_4_o6), .O7(main_4_o7), .Clk_out(main_4_clk_out), .Clk(main_3_clk_out));
  Game_screen_main main_5 (
    .Animation_Clock(main_4_clk_out), .Key_impulse(Key_impulse), .Reset__tree(RstRgr), .Out_0(main_5_out_0),
    .Out_1(main_5_out_1), .Out_2(main_5_out_2), .Out_3(main_5_out_3), .Out_4(main_5_out_4),
    .Out_5(main_5_out_5), .Out_6(main_5_out_6), .Out_7(main_5_out_7), .Input(main_4_register_out),
    .in_5(RstRgr), .Clk_out(main_5_clk_out), .Reg_out(main_5_reg_out));
  Timberman_or_tree_8_ROMs_main main_6 (
    .Animation_Clock(main_5_clk_out), .Key_impulse(1'b1), .Reset__tree(or_1_out),
    .Register_address(main_1_out), .Out_0(main_6_out_0), .Out_1(main_6_out_1), .Out_2(main_6_out_2),
    .Out_3(main_6_out_3), .Out_4(main_6_out_4), .Out_5(main_6_out_5), .Out_6(main_6_out_6),
    .Out_7(main_6_out_7), .Input(main_5_reg_out), .Key_selection(D));
  not not_1 (not_1_out, Display_ready);
  Hex_Digit_Display hex_digit_display_1 (.value(HS4));  // open: dp
  Hex_Digit_Display hex_digit_display_2 (.value(H4));  // open: dp
  DotMatrix #(.inputtype("row"), .matrixcols(24), .matrixrows(8)) dotmatrix_1 (
    .row0(main_2_o0), .row1(main_2_o1), .row2(main_2_o2), .row3(main_2_o3), .row4(main_2_o4),
    .row5(main_2_o5), .row6(main_2_o6), .row7(main_2_o7));
  DotMatrix #(.inputtype("row"), .matrixcols(24), .matrixrows(32)) dotmatrix_2 (
    .row0(main_3_out_0), .row1(main_3_out_1), .row2(main_3_out_2), .row3(main_3_out_3), .row4(main_3_out_4),
    .row5(main_3_out_5), .row6(main_3_out_6), .row7(main_3_out_7), .row8(main_4_o0), .row9(main_4_o1),
    .row10(main_4_o2), .row11(main_4_o3), .row12(main_4_o4), .row13(main_4_o5), .row14(main_4_o6),
    .row15(main_4_o7), .row16(main_5_out_0), .row17(main_5_out_1), .row18(main_5_out_2),
    .row19(main_5_out_3), .row20(main_5_out_4), .row21(main_5_out_5), .row22(main_5_out_6),
    .row23(main_5_out_7), .row24(main_6_out_0), .row25(main_6_out_1), .row26(main_6_out_2),
    .row27(main_6_out_3), .row28(main_6_out_4), .row29(main_6_out_5), .row30(main_6_out_6),
    .row31(main_6_out_7));
  DotMatrix #(.matrixcols(32), .matrixrows(1)) dotmatrix_3 (
    .col0(Timer[31]), .col1(Timer[30]), .col2(Timer[29]), .col3(Timer[28]), .col4(Timer[27]),
    .col5(Timer[26]), .col6(Timer[25]), .col7(Timer[24]), .col8(Timer[23]), .col9(Timer[22]),
    .col10(Timer[21]), .col11(Timer[20]), .col12(Timer[19]), .col13(Timer[18]), .col14(Timer[17]),
    .col15(Timer[16]), .col16(Timer[15]), .col17(Timer[14]), .col18(Timer[13]), .col19(Timer[12]),
    .col20(Timer[11]), .col21(Timer[10]), .col22(Timer[9]), .col23(Timer[8]), .col24(Timer[7]),
    .col25(Timer[6]), .col26(Timer[5]), .col27(Timer[4]), .col28(Timer[3]), .col29(Timer[2]),
    .col30(Timer[1]), .col31(Timer[0]));
  Pull_Resistor pull_resistor_1 (.node(pull_resistor_1_node));
  assign pull_resistor_1_node = keyboard_1_avail ? CLK_IN : 1'bz;  // Controlled_Buffer controlled_buffer_1
  Hex_Digit_Display hex_digit_display_3 (.value(HS3));  // open: dp
  Hex_Digit_Display hex_digit_display_4 (.value(H3));  // open: dp
  Keyboard keyboard_1 (
    .clk(pull_resistor_1_node), .re(Display_ready), .clr(not_1_out), .avail(keyboard_1_avail),
    .data(keyboard_1_data));
  Hex_Digit_Display hex_digit_display_5 (.value(HS2));  // open: dp
  Hex_Digit_Display hex_digit_display_6 (.value(H2));  // open: dp
  Clock Main_clk (.out(Main_clk_out));
  D_Flip_Flop d_ff_1 (.clk(linia1), .D(d_ff_1_qn), .Q(d_ff_1_q), .Qn(d_ff_1_qn));  // open: preset, en, reset
  Hex_Digit_Display hex_digit_display_7 (.value(HS1));  // open: dp
  Hex_Digit_Display hex_digit_display_8 (.value(H1));  // open: dp
  and and_1 (CLK_IN, Main_clk_out, d_ff_1_q);
  Clock clock_1 (.out(clock_1_out));
  Stop_countera_main main_7 (.Clk(CLK_ANIM), .Reset(Key_impulse), .Counter(Counter));
  Button button_1 (.out(Timber));
  Key_recognition_main main_8 (
    .Keyboard_input(keyboard_1_data), .Out(key), .Clk(CLK_IN), .A(A), .D(D), .KeyImpulse(Key_impulse));
  Random #(.width(3)) random_1 (.clk(clock_1_out), .out(random_1_out));  // open: next, clr
  Comparator #(.width(3)) comparator_1 (.a(Counter), .b(3'b000), .eq(Display_ready));  // open: gt, lt
  assign bit_extender_1_out = {{1{1'b0}}, key};  // Bit_Extender bit_extender_1
  Button Start (.out(linia1));
  Button button_2 (.out(Napoleon));
  Button button_3 (.out(Alien));
  Clock #(.highDuration(4), .lowDuration(4)) Animation_clk (.out(CLK_ANIM));
  Divider #(.width(3)) divider_1 (.a(random_1_out), .b(3'b011), .rem(divider_1_rem));  // open: out, upper
  Comparator #(.width(3)) comparator_2 (
    .a(bit_extender_1_out), .b(Kolizja_tree), .eq(comparator_2_eq));  // open: gt, lt
  Shift_Register #(.width(3), .length(5)) shift_register_1 (
    .in(divider_1_rem), .clk(Display_ready), .out(shift_register_1_out), .clr(RstRgr), .q0(SR1), .q1(SR2),
    .q2(SR3), .q3(SR4), .q4(SR5));  // open: shift, load, d0, d1, d2, d3, d4
  ROM_Tree_main main_9 (.Counter(Counter), .ROM_0(ROM0), .ROM_1(ROM1), .ROM_2(ROM2), .ROM_3(ROM_3), .ROM_4(ROM_4));
  Shift_register_rom_control_main main_10 (
    .in_1(ROM0), .in_2(ROM1), .in_3(ROM2), .in_4(ROM_3), .in_5(ROM_4), .Output(RegOut), .Address(SR1));  // open: in_6, in_7, in_8
  and and_2 (and_2_out, Display_ready, comparator_2_eq);
  Button button_4 (.out(button_4_out));
  not not_2 (not_2_out, comparator_2_eq);
  and and_3 (Scored, not_2_out, Display_ready);
  Shift_Register #(.width(3), .length(1)) shift_register_2 (
    .in(shift_register_1_out), .clk(Display_ready), .out(Kolizja_tree), .clr(Key_impulse));  // open: shift, load, d0, q0
  D_Flip_Flop d_ff_2 (.clk(TIMEOUT), .D(TIMEOUT), .Q(d_ff_2_q), .reset(Key_impulse));  // open: Qn, preset, en
  or or_2 (RstRgr, and_2_out, d_ff_2_q, button_4_out);
  or or_3 (or_3_out, RESET, RstRgr);
  or or_4 (or_4_out, RESET, RstRgr);
  Button button_5 (.out(RESET));
  PointCounter_main main_11 (
    .ADD(Scored), .RESET(or_3_out), .X000(H4), ._0X00(H3), ._00X0(H2), ._000X(H1), .Points(Points_value));  // open: LIMIT
  TIMEDISPLAY_main main_12 (
    .WHEN_1__SUB_TIME_ONE_TICK__WHEN_0_ADD_TIME_ON_TICK(Scored), .CLK(main_13_clk_timebar), .RESET(or_4_out),
    .OutputScreen(Timer), .TIME_OUT(TIMEOUT));
  Dynamic_difficulty_control_main main_13 (
    .Points_value(Points_value), .Clk_timebar(main_13_clk_timebar), .Stop(d_ff_3_q));
  D_Flip_Flop d_ff_3 (.clk(linia1), .D(d_ff_3_qn), .Q(d_ff_3_q), .Qn(d_ff_3_qn));  // open: preset, en, reset
  ScoreHolder_main main_14 (
    .CurrentPoints(Points_value), .CLK(CLK_IN), .X000(HS4), ._0X00(HS3), ._00X0(HS2), ._000X(HS1));  // open: RESET

  // Other names for the same wires on the sheet: Start_Stop = linia1

  // Notes on the sheet:
  //   Najwyższy wynik
  //   Obecny wynik
  //   Iterowanie po ROMie
  //   System kolizji
  //   Losowanie następnego segmentu drzewa
  //   oraz informacja do obsługi kolizji
  //   Wyświetlanie segmentów drzewa
  //   Optymalne taktowanie - 256 Hz (ewentualnie 512 Hz)
  //   Licznik punktów
  //   Licznik pozostałego czasu gry
endmodule
